// Logisim project TallerLogica-Combinatorios.circ as structural Verilog: 9 circuits, main circuit verificador
module sumador_simple (
  input  a,
  input  b,
  output S,
  output Cout
);

  xor xor_1 (S, a, b);
  and and_1 (Cout, a, b);
endmodule

module sumador_completo (
  input  Cin,
  input  A,
  input  B,
  output S,
  output Cout
);

  wire sumador_simple_1_cout, sumador_simple_2_cout, sumador_simple_2_s;

  sumador_simple sumador_simple_1 (.a(Cin), .b(sumador_simple_2_s), .S(S), .Cout(sumador_simple_1_cout));
  sumador_simple sumador_simple_2 (.a(A), .b(B), .S(sumador_simple_2_s), .Cout(sumador_simple_2_cout));
  or or_1 (Cout, sumador_simple_1_cout, sumador_simple_2_cout);
endmodule

module sumador_4 (
  input  Cin,
  input  [3:0] A,
  input  [3:0] B,
  output [3:0] S,
  output Cout
);

  wire sumador_completo_1_cout, sumador_completo_2_cout, sumador_completo_3_cout;

  sumador_completo sumador_completo_1 (.A(A[0]), .B(B[0]), .Cin(Cin), .S(S[0]), .Cout(sumador_completo_1_cout));
  sumador_completo sumador_completo_2 (
    .A(A[1]), .B(B[1]), .Cin(sumador_completo_1_cout), .S(S[1]), .Cout(sumador_completo_2_cout));
  sumador_completo sumador_completo_3 (
    .A(A[2]), .B(B[2]), .Cin(sumador_completo_2_cout), .S(S[2]), .Cout(sumador_completo_3_cout));
  sumador_completo sumador_completo_4 (.A(A[3]), .B(B[3]), .Cin(sumador_completo_3_cout), .S(S[3]), .Cout(Cout));
  Hex_Digit_Display hex_digit_display_1 (.value(S));  // open: dp
endmodule

module comparador_cero (
  input  [3:0] A,
  output Z
);

  nor nor_1 (Z, A[0], A[1], A[2], A[3]);
endmodule

module sumador_flags (
  input  Cin,
  input  [3:0] A,
  input  [3:0] B,
  output [3:0] S,
  output N,
  output Z,
  output V,
  output C
);

  wire xor_1_out;

  sumador_4 sumador_4_1 (.Cin(Cin), .A(A), .S(S), .B(B), .Cout(C));
  comparador_cero comparador_cero_1 (.A(S), .Z(Z));
  xor xor_1 (xor_1_out, A[3], B[3]);
  Hex_Digit_Display hex_digit_display_1 (.value(S));  // open: dp
  xor xor_2 (V, C, xor_1_out);
endmodule

module incrementador_4 (
  input  [3:0] A,
  output [3:0] S
);

  Hex_Digit_Display hex_digit_display_1 (.value(S));  // open: dp
endmodule

module inversor_4 (
  input  [3:0] A,
  input  INV,
  output [3:0] S
);

  Hex_Digit_Display hex_digit_display_1 (.value(S));  // open: dp
endmodule

module ALU (
  input  [3:0] A,
  input  [3:0] B,
  input  [1:0] OP,
  output N,
  output Z,
  output V,
  output C,
  output [3:0] S
);

  Hex_Digit_Display hex_digit_display_1 (.value(S));  // open: dp
endmodule

module verificador (
  output [3:0] a,
  output [3:0] b,
  output [1:0] Op,
  output N,
  output Z,
  output V,
  output C,
  output [3:0] Res,
  output halt
);

  wire clock_1_out;

  Clock clock_1 (.out(clock_1_out));
  Counter #(.width(10), .max('h3ff)) counter_1 (
    .Q({Op, b, a}), .carry(halt), .clk(clock_1_out));  // open: load, D, count, clr
  ALU alu_1 (.A(a), .B(b), .OP(Op), .N(N), .Z(Z), .V(V), .C(C), .S(Res));
endmodule
